// Logisim project modified.circ as structural Verilog: 5 circuits, main circuit main
module main (
  input  in_1
);

  wire alu_1_zeroflag, and_1_out, clear_count_out, clear_data_mem_out, clear_inst_mem_out, clock_1_out,
       controlunit_1_alusrc, controlunit_1_branch, controlunit_1_jr, controlunit_1_jump,
       controlunit_1_memread, controlunit_1_memtoreg, controlunit_1_memwrite, controlunit_1_regdst,
       controlunit_1_regwrite, not_1_out;
  wire [1:0] controlunit_1_aluop;
  wire [2:0] alucontrol_1_operational_code;
  wire [4:0] multiplexer_1_out;
  wire [23:0] alu_1_result, PC_q;
  wire [27:0] adder_1_out;
  wire [31:0] adder_2_out, bit_extender_1_out, bit_extender_2_out, multiplexer_2_out, multiplexer_3_out,
       multiplexer_4_out, multiplexer_5_out, multiplexer_6_out, ram_1_data, ram_2_data, regfile_1_read_data1,
       regfile_1_read_data2;
  wire [31:24] alu_1_result_2, PC_q_2;

  // Probe on multiplexer_6_out
  Clock clock_1 (.out(clock_1_out));
  Button clear_inst_mem (.out(clear_inst_mem_out));
  Button clear_count (.out(clear_count_out));
  Button clear_data_mem (.out(clear_data_mem_out));
  Register #(.width(32)) PC (
    .D(multiplexer_6_out), .en(in_1), .Q({PC_q_2, PC_q}), .clk(clock_1_out), .clr(clear_count_out));
  // Probe on PC_q
  // Probe on {PC_q_2, PC_q}
  Adder #(.width(32)) adder_1 (
    .a({PC_q_2, PC_q}), .b(32'h1), .out({bit_extender_1_out[31:28], adder_1_out}));  // open: cin, cout
  // Probe on ram_1_data[31:26]
  RAM #(.addrWidth(24), .dataWidth(32)) ram_1 (
    .addr(PC_q), .data(ram_1_data), .clk(clock_1_out), .ld(in_1), .clr(clear_inst_mem_out));  // open: sel
  // Probe on ram_1_data[15:0]
  // Probe on ram_1_data[20:16]
  assign bit_extender_1_out[27:0] = {{2{1'b0}}, ram_1_data[25:0]};  // Bit_Extender bit_extender_1
  // Probe on ram_1_data[25:21]
  Multiplexer #(.width(5), .enable("false")) multiplexer_1 (
    .in0(ram_1_data[20:16]), .in1(ram_1_data[15:11]), .out(multiplexer_1_out), .sel(controlunit_1_regdst));
  // Probe on multiplexer_1_out
  // Probe on ram_1_data[15:0]
  // Probe on {bit_extender_1_out[31:28], adder_1_out}
  assign bit_extender_2_out = {{16{ram_1_data[15]}}, ram_1_data[15:0]};  // Bit_Extender bit_extender_2
  LED jr (.in(controlunit_1_jr));
  LED jump (.in(controlunit_1_jump));
  ControlUnit controlunit_1 (
    .function_0_5(ram_1_data[5:0]), .Instruction_31_26(ram_1_data[31:26]), .RegWrite(controlunit_1_regwrite),
    .RegDst(controlunit_1_regdst), .ALUsrc(controlunit_1_alusrc), .ALUOp(controlunit_1_aluop),
    .MemRead(controlunit_1_memread), .MemWrite(controlunit_1_memwrite), .MemToReg(controlunit_1_memtoreg),
    .Branch(controlunit_1_branch), .Jump(controlunit_1_jump), .Jr(controlunit_1_jr));
  RegFile regfile_1 (
    .ReadReg1(ram_1_data[25:21]), .ReadReg2(ram_1_data[20:16]), .Write(controlunit_1_regwrite),
    .clock(clock_1_out), .Write_data(multiplexer_5_out), .Write_register(multiplexer_1_out),
    .Read_Data1(regfile_1_read_data1), .Read_Data2(regfile_1_read_data2));
  // Probe on bit_extender_2_out
  // Probe on alucontrol_1_operational_code
  LED branch (.in(controlunit_1_branch));
  // Probe on regfile_1_read_data2
  // Probe on bit_extender_2_out
  LED memtoreg (.in(controlunit_1_memtoreg));
  LED memwrite (.in(controlunit_1_memwrite));
  Multiplexer #(.width(32), .enable("false")) multiplexer_2 (
    .in0(regfile_1_read_data2), .in1(bit_extender_2_out), .out(multiplexer_2_out), .sel(controlunit_1_alusrc));
  // Probe on multiplexer_2_out
  ALUControl alucontrol_1 (
    ._5_0bits(ram_1_data[5:0]), .Operational_code(alucontrol_1_operational_code), .ALUOp(controlunit_1_aluop));
  LED memread (.in(controlunit_1_memread));
  // Probe on regfile_1_read_data1
  LED regdst (.in(controlunit_1_regdst));
  LED alusrc (.in(controlunit_1_alusrc));
  // Probe on alu_1_zeroflag
  ALU alu_1 (
    .readData1(regfile_1_read_data1), .readData2(multiplexer_2_out), .ALUop(alucontrol_1_operational_code),
    .Zeroflag(alu_1_zeroflag), .result({alu_1_result_2, alu_1_result}));  // open: out_6
  // Probe on regfile_1_read_data2
  // Probe on {bit_extender_1_out[31:28], adder_1_out}
  LED regwrite (.in(controlunit_1_regwrite));
  Adder #(.width(32)) adder_2 (
    .a({bit_extender_1_out[31:28], adder_1_out}), .b(bit_extender_2_out), .out(adder_2_out));  // open: cin, cout
  // Probe on alu_1_result
  // Probe on and_1_out
  Multiplexer #(.width(32), .enable("false")) multiplexer_3 (
    .in0({bit_extender_1_out[31:28], adder_1_out}), .in1(adder_2_out), .out(multiplexer_3_out),
    .sel(and_1_out));
  // Probe on ram_2_data
  RAM #(.addrWidth(24), .dataWidth(32), .bus("separate")) ram_2 (
    .addr(alu_1_result), .din(regfile_1_read_data2), .data(ram_2_data), .str(controlunit_1_memwrite),
    .clk(clock_1_out), .ld(controlunit_1_memread), .clr(clear_data_mem_out));  // open: sel
  Multiplexer #(.width(32), .enable("false")) multiplexer_4 (
    .in0(multiplexer_3_out), .in1(bit_extender_1_out), .out(multiplexer_4_out), .sel(controlunit_1_jump));
  and and_1 (and_1_out, controlunit_1_branch, alu_1_zeroflag);
  // Probe on {alu_1_result_2, alu_1_result}
  // Probe on regfile_1_read_data1
  not not_1 (not_1_out, controlunit_1_jr);
  Multiplexer #(.width(32), .enable("false")) multiplexer_5 (
    .in0({alu_1_result_2, alu_1_result}), .in1(ram_2_data), .out(multiplexer_5_out),
    .sel(controlunit_1_memtoreg));
  // Probe on multiplexer_5_out
  Multiplexer #(.width(32), .enable("false")) multiplexer_6 (
    .in0(regfile_1_read_data1), .in1(multiplexer_4_out), .out(multiplexer_6_out), .sel(not_1_out));

  // Notes on the sheet:
  //   PC+1
  //   Instruction [25-0]
  //   26
  //   28
  //   reg dst
  //   PC+1[31-28]
  //   Jump Address [31-0]
  //   ALUsrc
  //   Branch
  //   Jump
endmodule

module RegFile (
  input  [4:0] ReadReg1,
  input  [4:0] ReadReg2,
  input  Write,
  input  clock,
  input  [31:0] Write_data,
  input  [4:0] Write_register,
  output [31:0] Read_Data1,
  output [31:0] Read_Data2
);

  wire and_1_out, and_2_out, and_3_out, and_4_out, and_5_out, and_6_out, and_7_out, and_8_out, and_9_out,
       and_10_out, and_11_out, and_12_out, and_13_out, and_14_out, and_15_out, and_16_out, and_17_out,
       and_18_out, and_19_out, and_20_out, and_21_out, and_22_out, and_23_out, and_24_out, and_25_out,
       and_26_out, and_27_out, and_28_out, and_29_out, and_30_out, and_31_out, and_32_out, decoder_1_out0,
       decoder_1_out1, decoder_1_out2, decoder_1_out3, decoder_1_out4, decoder_1_out5, decoder_1_out6,
       decoder_1_out7, decoder_1_out8, decoder_1_out9, decoder_1_out10, decoder_1_out11, decoder_1_out12,
       decoder_1_out13, decoder_1_out14, decoder_1_out15, decoder_1_out16, decoder_1_out17, decoder_1_out18,
       decoder_1_out19, decoder_1_out20, decoder_1_out21, decoder_1_out22, decoder_1_out23, decoder_1_out24,
       decoder_1_out25, decoder_1_out26, decoder_1_out27, decoder_1_out28, decoder_1_out29, decoder_1_out30,
       decoder_1_out31;
  wire [31:0] _0_q, _1_q, _2_q, _3_q, _4_q, _5_q, _6_q, _7_q, _8_q, _9_q, _10_q, _11_q, _12_q, _13_q, _14_q,
       _15_q, _16_q, _17_q, _18_q, _19_q, _20_q, _21_q, _22_q, _23_q, _24_q, _25_q, _26_q, _27_q, _28_q,
       _29_q, _30_q, _31_q;

  Decoder #(.select(5), .enable("false")) decoder_1 (
    .out0(decoder_1_out0), .out1(decoder_1_out1), .out2(decoder_1_out2), .out3(decoder_1_out3),
    .out4(decoder_1_out4), .out5(decoder_1_out5), .out6(decoder_1_out6), .out7(decoder_1_out7),
    .out8(decoder_1_out8), .out9(decoder_1_out9), .out10(decoder_1_out10), .out11(decoder_1_out11),
    .out12(decoder_1_out12), .out13(decoder_1_out13), .out14(decoder_1_out14), .out15(decoder_1_out15),
    .out16(decoder_1_out16), .out17(decoder_1_out17), .out18(decoder_1_out18), .out19(decoder_1_out19),
    .out20(decoder_1_out20), .out21(decoder_1_out21), .out22(decoder_1_out22), .out23(decoder_1_out23),
    .out24(decoder_1_out24), .out25(decoder_1_out25), .out26(decoder_1_out26), .out27(decoder_1_out27),
    .out28(decoder_1_out28), .out29(decoder_1_out29), .out30(decoder_1_out30), .out31(decoder_1_out31),
    .sel(Write_register));
  and and_1 (and_1_out, Write, decoder_1_out0);
  and and_2 (and_2_out, Write, decoder_1_out1);
  and and_3 (and_3_out, Write, decoder_1_out2);
  and and_4 (and_4_out, Write, decoder_1_out3);
  and and_5 (and_5_out, Write, decoder_1_out4);
  and and_6 (and_6_out, Write, decoder_1_out5);
  and and_7 (and_7_out, Write, decoder_1_out6);
  and and_8 (and_8_out, Write, decoder_1_out7);
  and and_9 (and_9_out, Write, decoder_1_out8);
  and and_10 (and_10_out, Write, decoder_1_out9);
  and and_11 (and_11_out, Write, decoder_1_out10);
  and and_12 (and_12_out, Write, decoder_1_out11);
  and and_13 (and_13_out, Write, decoder_1_out12);
  and and_14 (and_14_out, Write, decoder_1_out13);
  and and_15 (and_15_out, Write, decoder_1_out14);
  and and_16 (and_16_out, Write, decoder_1_out15);
  and and_17 (and_17_out, Write, decoder_1_out16);
  and and_18 (and_18_out, Write, decoder_1_out17);
  and and_19 (and_19_out, Write, decoder_1_out18);
  and and_20 (and_20_out, Write, decoder_1_out19);
  and and_21 (and_21_out, Write, decoder_1_out20);
  and and_22 (and_22_out, Write, decoder_1_out21);
  and and_23 (and_23_out, Write, decoder_1_out22);
  and and_24 (and_24_out, Write, decoder_1_out23);
  and and_25 (and_25_out, Write, decoder_1_out24);
  and and_26 (and_26_out, Write, decoder_1_out25);
  and and_27 (and_27_out, Write, decoder_1_out26);
  and and_28 (and_28_out, Write, decoder_1_out27);
  and and_29 (and_29_out, Write, decoder_1_out28);
  and and_30 (and_30_out, Write, decoder_1_out29);
  and and_31 (and_31_out, Write, decoder_1_out30);
  and and_32 (and_32_out, Write, decoder_1_out31);
  Register #(.width(32)) _0 (.D(Write_data), .en(and_1_out), .Q(_0_q), .clk(clock));  // open: clr
  Register #(.width(32)) _1 (.D(Write_data), .en(and_2_out), .Q(_1_q), .clk(clock));  // open: clr
  Register #(.width(32)) _2 (.D(Write_data), .en(and_3_out), .Q(_2_q), .clk(clock));  // open: clr
  Register #(.width(32)) _3 (.D(Write_data), .en(and_4_out), .Q(_3_q), .clk(clock));  // open: clr
  Register #(.width(32)) _4 (.D(Write_data), .en(and_5_out), .Q(_4_q), .clk(clock));  // open: clr
  Register #(.width(32)) _5 (.D(Write_data), .en(and_6_out), .Q(_5_q), .clk(clock));  // open: clr
  Register #(.width(32)) _6 (.D(Write_data), .en(and_7_out), .Q(_6_q), .clk(clock));  // open: clr
  Register #(.width(32)) _7 (.D(Write_data), .en(and_8_out), .Q(_7_q), .clk(clock));  // open: clr
  Register #(.width(32)) _8 (.D(Write_data), .en(and_9_out), .Q(_8_q), .clk(clock));  // open: clr
  Register #(.width(32)) _9 (.D(Write_data), .en(and_10_out), .Q(_9_q), .clk(clock));  // open: clr
  Register #(.width(32)) _10 (.D(Write_data), .en(and_11_out), .Q(_10_q), .clk(clock));  // open: clr
  Register #(.width(32)) _11 (.D(Write_data), .en(and_12_out), .Q(_11_q), .clk(clock));  // open: clr
  Register #(.width(32)) _12 (.D(Write_data), .en(and_13_out), .Q(_12_q), .clk(clock));  // open: clr
  Register #(.width(32)) _13 (.D(Write_data), .en(and_14_out), .Q(_13_q), .clk(clock));  // open: clr
  Register #(.width(32)) _14 (.D(Write_data), .en(and_15_out), .Q(_14_q), .clk(clock));  // open: clr
  Register #(.width(32)) _15 (.D(Write_data), .en(and_16_out), .Q(_15_q), .clk(clock));  // open: clr
  Register #(.width(32)) _16 (.D(Write_data), .en(and_17_out), .Q(_16_q), .clk(clock));  // open: clr
  Register #(.width(32)) _17 (.D(Write_data), .en(and_18_out), .Q(_17_q), .clk(clock));  // open: clr
  Register #(.width(32)) _18 (.D(Write_data), .en(and_19_out), .Q(_18_q), .clk(clock));  // open: clr
  Register #(.width(32)) _19 (.D(Write_data), .en(and_20_out), .Q(_19_q), .clk(clock));  // open: clr
  Register #(.width(32)) _20 (.D(Write_data), .en(and_21_out), .Q(_20_q), .clk(clock));  // open: clr
  Register #(.width(32)) _21 (.D(Write_data), .en(and_22_out), .Q(_21_q), .clk(clock));  // open: clr
  Register #(.width(32)) _22 (.D(Write_data), .en(and_23_out), .Q(_22_q), .clk(clock));  // open: clr
  Register #(.width(32)) _23 (.D(Write_data), .en(and_24_out), .Q(_23_q), .clk(clock));  // open: clr
  Register #(.width(32)) _24 (.D(Write_data), .en(and_25_out), .Q(_24_q), .clk(clock));  // open: clr
  Register #(.width(32)) _25 (.D(Write_data), .en(and_26_out), .Q(_25_q), .clk(clock));  // open: clr
  Register #(.width(32)) _26 (.D(Write_data), .en(and_27_out), .Q(_26_q), .clk(clock));  // open: clr
  Register #(.width(32)) _27 (.D(Write_data), .en(and_28_out), .Q(_27_q), .clk(clock));  // open: clr
  Register #(.width(32)) _28 (.D(Write_data), .en(and_29_out), .Q(_28_q), .clk(clock));  // open: clr
  Register #(.width(32)) _29 (.D(Write_data), .en(and_30_out), .Q(_29_q), .clk(clock));  // open: clr
  Register #(.width(32)) _30 (.D(Write_data), .en(and_31_out), .Q(_30_q), .clk(clock));  // open: clr
  Register #(.width(32)) _31 (.D(Write_data), .en(and_32_out), .Q(_31_q), .clk(clock));  // open: clr
  Multiplexer #(.select(5), .width(32), .enable("false")) multiplexer_1 (
    .in0(_0_q), .in1(_1_q), .in2(_2_q), .in3(_3_q), .in4(_4_q), .in5(_5_q), .in6(_6_q), .in7(_7_q),
    .in8(_8_q), .in9(_9_q), .in10(_10_q), .in11(_11_q), .in12(_12_q), .in13(_13_q), .in14(_14_q),
    .in15(_15_q), .in16(_16_q), .in17(_17_q), .in18(_18_q), .in19(_19_q), .in20(_20_q), .in21(_21_q),
    .in22(_22_q), .in23(_23_q), .in24(_24_q), .in25(_25_q), .in26(_26_q), .in27(_27_q), .in28(_28_q),
    .in29(_29_q), .in30(_30_q), .in31(_31_q), .out(Read_Data1), .sel(ReadReg1));
  Multiplexer #(.select(5), .width(32), .enable("false")) multiplexer_2 (
    .in0(_0_q), .in1(_1_q), .in2(_2_q), .in3(_3_q), .in4(_4_q), .in5(_5_q), .in6(_6_q), .in7(_7_q),
    .in8(_8_q), .in9(_9_q), .in10(_10_q), .in11(_11_q), .in12(_12_q), .in13(_13_q), .in14(_14_q),
    .in15(_15_q), .in16(_16_q), .in17(_17_q), .in18(_18_q), .in19(_19_q), .in20(_20_q), .in21(_21_q),
    .in22(_22_q), .in23(_23_q), .in24(_24_q), .in25(_25_q), .in26(_26_q), .in27(_27_q), .in28(_28_q),
    .in29(_29_q), .in30(_30_q), .in31(_31_q), .out(Read_Data2), .sel(ReadReg2));
endmodule

module ControlUnit (
  input  [5:0] Instruction_31_26,
  input  [5:0] function_0_5,
  output RegWrite,
  output ALUsrc,
  output MemRead,
  output MemToReg,
  output Jump,
  output RegDst,
  output [1:0] ALUOp,
  output MemWrite,
  output Branch,
  output Jr
);

  wire and_2_out, Jr_out, not_1_out, not_2_out, not_3_out, not_4_out, not_5_out, Op0_out, Op1_out, Op2_out,
       Op3_out, Op4_out, Op5_out;

  not Op4 (Op4_out, Instruction_31_26[4]);
  not Op5 (Op5_out, Instruction_31_26[5]);
  not Op2 (Op2_out, Instruction_31_26[2]);
  not Op3 (Op3_out, Instruction_31_26[3]);
  not Op1 (Op1_out, Instruction_31_26[1]);
  not Op0 (Op0_out, Instruction_31_26[0]);
  and u_Jr (Jr_out, Op5_out, Op4_out, Op3_out, Op2_out, Op1_out, Op0_out);
  and R (ALUOp[1], Op5_out, Op4_out, Op3_out, Op2_out, Op1_out, Op0_out);
  and lw (MemRead, Instruction_31_26[5], Op4_out, Op3_out, Op2_out, Instruction_31_26[1], Instruction_31_26[0]);
  and sw (MemWrite, Instruction_31_26[5], Op4_out, Instruction_31_26[3], Op2_out, Instruction_31_26[1], Instruction_31_26[0]);
  and beq (ALUOp[0], Op5_out, Op4_out, Op3_out, Instruction_31_26[2], Op1_out, Op0_out);
  and j (Jump, Op5_out, Op4_out, Op3_out, Op2_out, Instruction_31_26[1], Op0_out);
  or or_1 (RegWrite, ALUOp[1], MemRead);
  or or_2 (ALUsrc, MemRead, MemWrite);
  not not_1 (not_1_out, function_0_5[0]);
  not not_2 (not_2_out, function_0_5[1]);
  not not_3 (not_3_out, function_0_5[2]);
  not not_4 (not_4_out, function_0_5[4]);
  not not_5 (not_5_out, function_0_5[5]);
  and and_1 (Jr, Jr_out, and_2_out);
  and and_2 (and_2_out, not_1_out, not_2_out, not_3_out, function_0_5[3], not_4_out, not_5_out);

  assign Branch = ALUOp[0];
  assign MemToReg = MemRead;
  assign RegDst = ALUOp[1];
endmodule

module ALU (
  input  [31:0] readData1,
  input  [31:0] readData2,
  input  [2:0] ALUop,
  output Zeroflag,
  output [31:0] result,
  output out_6
);

  wire subtractor_2_bout;
  wire [31:0] adder_1_out, and_out, bit_extender_1_out, or_out, subtractor_1_out;

  assign and_out = readData1 & readData2;  // AND_Gate and, 32 bits wide
  assign or_out = readData1 | readData2;  // OR_Gate or, 32 bits wide
  Adder #(.width(32)) adder_1 (.a(readData1), .b(readData2), .out(adder_1_out));  // open: cin, cout
  Subtractor #(.width(32)) subtractor_1 (
    .a(readData1), .b(readData2), .out(subtractor_1_out), .bout(out_6));  // open: bin
  Subtractor #(.width(32)) subtractor_2 (
    .a(readData1), .b(readData2), .bin(1'b0), .bout(subtractor_2_bout));  // open: out
  assign bit_extender_1_out = {{31{1'b0}}, subtractor_2_bout};  // Bit_Extender bit_extender_1
  Multiplexer #(.select(3), .width(32)) multiplexer_1 (
    .in0(and_out), .in1(or_out), .in2(adder_1_out), .in6(subtractor_1_out), .in7(bit_extender_1_out),
    .out(result), .sel(ALUop));  // open: in3, in4, in5, en
  nor nor_1 (Zeroflag, result[0], result[1], result[2], result[3], result[4], result[5], result[6], result[7], result[8], result[9], result[10], result[11], result[12], result[13], result[14], result[15], result[16], result[17], result[18], result[19], result[20], result[21], result[22], result[23], result[24], result[25], result[26], result[27], result[28], result[29], result[30], result[31]);
endmodule

module ALUControl (
  input  [1:0] ALUOp,
  input  [5:0] _5_0bits,
  output [2:0] Operational_code
);

  wire and_1_out, or_1_out;

  or or_1 (or_1_out, _5_0bits[3], _5_0bits[0]);
  and and_1 (and_1_out, ALUOp[1], _5_0bits[1]);
  or or_2 (Operational_code[2], ALUOp[0], and_1_out);
  or or_3 (Operational_code[1], ~ALUOp[1], ~_5_0bits[2]);  // OR_Gate
  and and_2 (Operational_code[0], ALUOp[1], or_1_out);
endmodule
